# Fritzing sketch progr_Attiny (saved by Fritzing 0.8.7b)
circuit board: 8.46667cm x 5.64444cm
breadboards: 1

parts:
  hBeat = LED - 5mm [color="Red (633nm)" package="5 mm [THT]"]
  error = LED - 5mm [color="Red (633nm)" package="5 mm [THT]"]
  Progr = LED - 5mm [color="Red (633nm)" package="5 mm [THT]"]
  R1 = Resistor [tolerance=±5% resistance=220 package=THT]
  R2 = Resistor [tolerance=±5% resistance=220 package=THT]
  R3 = Resistor [tolerance=±5% resistance=220 package=THT]
  attiny84 = IC, DIP package, 14 pins [chip_label=Attiny84]
  attiny4313 = IC, DIP package, 20 pins [chip_label=Attiny4313]
  programAttiny = Arduino Uno (Rev3)

nets:
  N1: hBeat.cathode, R1.Pin_1
  N2: hBeat.anode, programAttiny.D9_PWM
  N3: error.cathode, R2.Pin_1
  N4: error.anode, programAttiny.D8
  N5: Progr.cathode, R3.Pin_1
  N6: Progr.anode, programAttiny.D7
  N7: R1.Pin_0, R2.Pin_0, R3.Pin_0, attiny84.pin14, programAttiny.GND
  N8: attiny84.pin1, attiny4313.pin20, programAttiny.5V
  N9: attiny84.pin4, programAttiny.D10_PWM/SS
  N10: attiny84.pin7, attiny4313.pin17, programAttiny.D11_PWM/MOSI
  N11: attiny84.pin8, programAttiny.D12/MISO
  N12: attiny84.pin9, attiny4313.pin19, programAttiny.D13/SCK
